# Fritzing sketch cablage (saved by Fritzing 0.9.3b)
breadboards: 1

parts:
  Raspberry_Pi_1 = Raspberry Pi 3 [part_number=RPI-3-V1.2]
  S1 = Round Pushbutton
  S2 = Round Pushbutton
  LED1 = LED - 3mm [color="White (4500K)" package="3 mm [THT]"]
  R1 = Resistor [tolerance=±5% resistance=330 package=THT]
  R2 = Resistor [tolerance=±5% resistance=330 package=THT]
  LED2 = LED - 3mm [color="Red (660nm)" package="3 mm [THT]"]
  R3 = Resistor [tolerance=±5% resistance=330 package=THT]
  LED3 = LED - 3mm [color="Yellow (595nm)" package="3 mm [THT]"]

nets:
  N1: Raspberry_Pi_1.GPIO3, S1.leg1
  N2: Raspberry_Pi_1.GIPO17, S2.leg1
  N3: Raspberry_Pi_1.GIPO12, R3.Pin_0
  N4: Raspberry_Pi_1.GIPO18, R1.Pin_0
  N5: Raspberry_Pi_1.GIPO14, R2.Pin_0
  N6: Raspberry_Pi_1.GND, S1.leg0, S2.leg0, LED1.cathode, LED2.cathode, LED3.cathode
  N7: LED1.anode, R1.Pin_1
  N8: R2.Pin_1, LED2.anode
  N9: R3.Pin_1, LED3.anode

notes:
  on/off
  photo
  power
  activity
  activity 2
